# Fritzing sketch AutoRes II (saved by Fritzing 0.9.3b)
breadboards: 1

parts:
  R1 = Resistor [tolerance=±5% resistance=300 package=THT]
  R2 = Resistor [tolerance=±5% resistance=300 package=THT]
  R3 = Resistor [tolerance=±5% resistance=300 package=THT]
  R4 = Resistor [tolerance=±5% resistance=300 package=THT]
  R5 = Resistor [tolerance=±5% resistance=300 package=THT]
  R6 = Resistor [tolerance=±5% resistance=300 package=THT]
  LED1 = RGB LED (com. cathode, rbg) [package="5 mm [THT]"]
  LED2 = RGB LED (com. cathode, rbg) [package="5 mm [THT]"]
  J1 = Piezo Speaker
  DHT1 = DHT11 Humitidy and Temperature Sensor
  R8 = Resistor [tolerance=±5% resistance=10k package=THT]
  PIR1 = PIR sensor
  LED3 = RGB LED (com. cathode, rbg) [package="5 mm [THT]"]
  LED4 = RGB LED (com. cathode, rbg) [package="5 mm [THT]"]
  R9 = Resistor [tolerance=±5% resistance=300 package=THT]
  R10 = Resistor [tolerance=±5% resistance=300 package=THT]
  R11 = Resistor [tolerance=±5% resistance=300 package=THT]
  R12 = Resistor [tolerance=±5% resistance=300 package=THT]
  R13 = Resistor [tolerance=±5% resistance=300 package=THT]
  R14 = Resistor [tolerance=±5% resistance=300 package=THT]
  Componente2 = Arduino Uno (Rev3)
  Componente3 = Bluetooth HC-05
  R15 = Resistor [tolerance=±5% resistance=300 package=THT]
  R16 = Resistor [tolerance=±5% resistance=300 package=THT]
  R17 = Resistor [tolerance=±5% resistance=300 package=THT]

nets:
  N1: R1.Pin_0, LED1.red_anode
  N2: R1.Pin_1, Componente2.D13/SCK
  N3: R2.Pin_0, LED1.green_anode
  N4: R2.Pin_1, Componente2.D12/MISO
  N5: R3.Pin_0, LED1.blue_anode
  N6: R3.Pin_1, Componente2.D11_PWM/MOSI
  N7: R4.Pin_0, LED2.red_anode
  N8: R4.Pin_1, Componente2.D10_PWM/SS
  N9: R5.Pin_0, LED2.green_anode
  N10: R5.Pin_1, Componente2.D9_PWM
  N11: R6.Pin_0, LED2.blue_anode
  N12: R6.Pin_1, Componente2.D8
  GND: LED1.common_cathode, LED2.common_cathode, J1.pin1, DHT1.GND, PIR1.GND, LED3.common_cathode, LED4.common_cathode, Componente2.GND, Componente3.GND, R17.Pin_0
  N13: J1.pin2, Componente2.A4/SDA
  VDD: DHT1.VDD, R8.Pin_1, PIR1.VDD, Componente2.5V, Componente3.VCC
  N14: DHT1.DATA, R8.Pin_0, Componente2.A5/SCL
  N15: PIR1.SIG, Componente2.D4
  N16: LED3.red_anode, R9.Pin_0
  N17: LED3.blue_anode, R11.Pin_0
  N18: LED3.green_anode, R10.Pin_0
  N19: LED4.red_anode, R12.Pin_0
  N20: LED4.blue_anode, R14.Pin_0
  N21: LED4.green_anode, R13.Pin_0
  N22: R9.Pin_1, Componente2.D7
  N23: R10.Pin_1, Componente2.D6_PWM
  N24: R11.Pin_1, Componente2.D5_PWM
  N25: R12.Pin_1, Componente2.A0
  N26: R13.Pin_1, Componente2.A1
  N27: R14.Pin_1, Componente2.A2
  N28: Componente2.D2, Componente3.TXD
  N29: Componente2.D3_PWM, R15.Pin_0, R15.Pin_1, R16.Pin_1
  N30: Componente3.RXD, R16.Pin_0, R17.Pin_1

custom parts:
  DHT11 Humitidy and Temperature Sensor: DHT11 Humidity and Temperature Sensor

// code stored in the sketch: AutoRes II.ino
// Inclui a biblioteca DHT que possui as fun??es dos sensores do tipo DHT
#include "DHT.h"

#include <SoftwareSerial.h> // Comandos Seriais

SoftwareSerial HC05(2, 3); // TX-RX

// Declara??o dos pinos
const int pinoLEDR1 = 13;
const int pinoLEDG1 = 12;
const int pinoLEDB1 = 11;
const int pinoLEDR2 = 10;
const int pinoLEDG2 = 9;
const int pinoLEDB2 = 8;
const int pinoLEDR3 = 7;
const int pinoLEDG3 = 6;
const int pinoLEDB3 = 5;
const int pinoLEDR4 = A0;
const int pinoLEDG4 = A1;
const int pinoLEDB4 = A2;
const int pino_dht = A5;
const int pinoBuzzer = A4;

//variaveis
String dados;
String enviar;
String estado;
int n = 0;
bool stateA = false;

// Vari?vel para armazenar o valor de temperatura e umidade
float temperatura; 
float umidade;

DHT dht(pino_dht, DHT11); // define o pino e o tipo de DHT

// Definir pinos de conex?o:
#define pirPin 4
// Crie vari?veis:
int val = 0;
bool motionState = false; // Come?amos sem nenhum movimento detectado.
bool buzState = false;

void setup()
{
  // Inicia e configura a Serial
  Serial.begin(9600); // 9600bps
  
  HC05.begin(9600); // Taxa de transmiss?o do M?dulo
  
  dht.begin(); // inicializa o sensor DHT
  
  //Configura os pinos
  pinMode(pinoLEDR1, OUTPUT);
  pinMode(pinoLEDG1, OUTPUT);
  pinMode(pinoLEDB1, OUTPUT);
  pinMode(pinoLEDR2, OUTPUT);
  pinMode(pinoLEDG2, OUTPUT);
  pinMode(pinoLEDB2, OUTPUT);
  pinMode(pinoLEDR3, OUTPUT);
  pinMode(pinoLEDG3, OUTPUT);
  pinMode(pinoLEDB3, OUTPUT);
  pinMode(pinoLEDR4, OUTPUT);
  pinMode(pinoLEDG4, OUTPUT);
  pinMode(pinoLEDB4, OUTPUT);
  pinMode(pinoBuzzer, OUTPUT);
  pinMode(pirPin, INPUT);
}

void loop()
{
  if(HC05.available()>0){
    dados = HC05.readString();
    Serial.println(dados);
    delay(15);

    // ************** ALARME ***************
    if(dados == "ALARMEON"){
      buzState = false;
      stateA = true;
    }
    if(dados == "ALARMEOFF"){
      stateA = false;
      buzState = false;
    }
    
    // *************** LED's ***************
    // LIGAR/DESLIGAR LED's
    if (dados == "LED1ON"){
        digitalWrite(pinoLEDR1, HIGH);
        digitalWrite(pinoLEDG1, HIGH);
        digitalWrite(pinoLEDB1, HIGH);
    }
    if (dados == "LED1OFF"){
        digitalWrite(pinoLEDR1, LOW);
        digitalWrite(pinoLEDG1, LOW);
        digitalWrite(pinoLEDB1, LOW);
    }
    if (dados == "LED2ON"){
        digitalWrite(pinoLEDR2, HIGH);
        digitalWrite(pinoLEDG2, HIGH);
        digitalWrite(pinoLEDB2, HIGH);
    }
    if (dados == "LED2OFF"){
        digitalWrite(pinoLEDR2, LOW);
        digitalWrite(pinoLEDG2, LOW);
        digitalWrite(pinoLEDB2, LOW);
    }
    if (dados == "LED3ON"){
        digitalWrite(pinoLEDR3, HIGH);
        digitalWrite(pinoLEDG3, HIGH);
        digitalWrite(pinoLEDB3, HIGH);
    }
    if (dados == "LED3OFF"){
        digitalWrite(pinoLEDR3, LOW);
        digitalWrite(pinoLEDG3, LOW);
        digitalWrite(pinoLEDB3, LOW);
    }
    if (dados == "LED4ON"){
        digitalWrite(pinoLEDR4, HIGH);
        digitalWrite(pinoLEDG4, HIGH);
        digitalWrite(pinoLEDB4, HIGH);
    }
    if (dados == "LED4OFF"){
        digitalWrite(pinoLEDR4, LOW);
        digitalWrite(pinoLEDG4, LOW);
        digitalWrite(pinoLEDB4, LOW);
    }

    // CORES LED's
    
      // ########### LED1 ###########
    if (dados == "LED1B"){
        digitalWrite(pinoLEDR1, LOW);
        digitalWrite(pinoLEDG1, LOW);
        digitalWrite(pinoLEDB1, HIGH);
    }
    if (dados == "LED1P"){
        digitalWrite(pinoLEDR1, HIGH);
        digitalWrite(pinoLEDG1, LOW);
        digitalWrite(pinoLEDB1, HIGH);
    }
    if (dados == "LED1W"){
        digitalWrite(pinoLEDR1, HIGH);
        digitalWrite(pinoLEDG1, HIGH);
        digitalWrite(pinoLEDB1, HIGH);
    }
    if (dados == "LED1R"){
        digitalWrite(pinoLEDR1, HIGH);
        digitalWrite(pinoLEDG1, LOW);
        digitalWrite(pinoLEDB1, LOW);
    }
    if (dados == "LED1G"){
        digitalWrite(pinoLEDR1, LOW);
        digitalWrite(pinoLEDG1, HIGH);
        digitalWrite(pinoLEDB1, LOW);
    }
    if (dados == "LED1Y"){
        digitalWrite(pinoLEDR1, HIGH);
        digitalWrite(pinoLEDG1, HIGH);
        digitalWrite(pinoLEDB1, LOW);
    }
    
      // ########### LED2 ###########
    if (dados == "LED2B"){
        digitalWrite(pinoLEDR2, LOW);
        digitalWrite(pinoLEDG2, LOW);
        digitalWrite(pinoLEDB2, HIGH);
    }
    if (dados == "LED2P"){
        digitalWrite(pinoLEDR2, HIGH);
        digitalWrite(pinoLEDG2, LOW);
        digitalWrite(pinoLEDB2, HIGH);
    }
    if (dados == "LED2W"){
        digitalWrite(pinoLEDR2, HIGH);
        digitalWrite(pinoLEDG2, HIGH);
        digitalWrite(pinoLEDB2, HIGH);
    }
    if (dados == "LED2R"){
        digitalWrite(pinoLEDR2, HIGH);
        digitalWrite(pinoLEDG2, LOW);
        digitalWrite(pinoLEDB2, LOW);
    }
    if (dados == "LED2G"){
        digitalWrite(pinoLEDR2, LOW);
        digitalWrite(pinoLEDG2, HIGH);
        digitalWrite(pinoLEDB2, LOW);
    }
    if (dados == "LED2Y"){
        digitalWrite(pinoLEDR2, HIGH);
        digitalWrite(pinoLEDG2, HIGH);
        digitalWrite(pinoLEDB2, LOW);
    }
    
      // ########### LED3 ###########
    if (dados == "LED3B"){
        digitalWrite(pinoLEDR3, LOW);
        digitalWrite(pinoLEDG3, LOW);
        digitalWrite(pinoLEDB3, HIGH);
    }
    if (dados == "LED3P"){
        digitalWrite(pinoLEDR3, HIGH);
        digitalWrite(pinoLEDG3, LOW);
        digitalWrite(pinoLEDB3, HIGH);
    }
    if (dados == "LED3W"){
        digitalWrite(pinoLEDR3, HIGH);
        digitalWrite(pinoLEDG3, HIGH);
        digitalWrite(pinoLEDB3, HIGH);
    }
    if (dados == "LED3R"){
        digitalWrite(pinoLEDR3, HIGH);
        digitalWrite(pinoLEDG3, LOW);
        digitalWrite(pinoLEDB3, LOW);
    }
    if (dados == "LED3G"){
        digitalWrite(pinoLEDR3, LOW);
        digitalWrite(pinoLEDG3, HIGH);
        digitalWrite(pinoLEDB3, LOW);
    }
    if (dados == "LED3Y"){
        digitalWrite(pinoLEDR3, HIGH);
        digitalWrite(pinoLEDG3, HIGH);
        digitalWrite(pinoLEDB3, LOW);
    }

      // ########### LED4 ###########
    if (dados == "LED4B"){
        digitalWrite(pinoLEDR4, LOW);
        digitalWrite(pinoLEDG4, LOW);
        digitalWrite(pinoLEDB4, HIGH);
    }
    if (dados == "LED4P"){
        digitalWrite(pinoLEDR4, HIGH);
        digitalWrite(pinoLEDG4, LOW);
        digitalWrite(pinoLEDB4, HIGH);
    }
    if (dados == "LED4W"){
        digitalWrite(pinoLEDR4, HIGH);
        digitalWrite(pinoLEDG4, HIGH);
        digitalWrite(pinoLEDB4, HIGH);
    }
    if (dados == "LED4R"){
        digitalWrite(pinoLEDR4, HIGH);
        digitalWrite(pinoLEDG4, LOW);
        digitalWrite(pinoLEDB4, LOW);
    }
    if (dados == "LED4G"){
        digitalWrite(pinoLEDR4, LOW);
        digitalWrite(pinoLEDG4, HIGH);
        digitalWrite(pinoLEDB4, LOW);
    }
    if (dados == "LED4Y"){
        digitalWrite(pinoLEDR4, HIGH);
        digitalWrite(pinoLEDG4, HIGH);
        digitalWrite(pinoLEDB4, LOW);
    }
  }
  // Aguarda alguns segundos entre uma leitura e outra
  delay(2000); // 2 segundos (Datasheet)

  if (buzState == false){
        sensor();
  }
  
  if (stateA == true){
     // Leia o pirPin e armazene como val:
     val = digitalRead(pirPin);
     // Se o movimento for detectado (pirPin = HIGH), fa?a o seguinte:
     if (val == HIGH) {
        buzState = true;
        // Altere o estado de movimento para verdadeiro (movimento detectado):
        if (motionState == false) {
          Serial.println("Movimento detectado!");
          motionState = true;
        }
     } else {  // Se nenhum movimento for detectado (pirPin = LOW), fa?a o seguinte:
        // Altere o estado de movimento para falso (sem movimento):
        if (motionState == true) {
          Serial.println("Movimento finalizado!");
          motionState = false;
        }
      }
     if (buzState == true){
        alarm(500, 1000);
        delay(150);
     }
   }
  
}
void alarm(long duration, int freq) {
  tone(pinoBuzzer, 1000);
  estado = "MOVIMENTO SUSPEITO";
  enviar = (String)temperatura + "," + (String)umidade + "," + estado;
  HC05.println(enviar);
  digitalWrite(pinoLEDR1, HIGH);
  digitalWrite(pinoLEDG1, LOW);
  digitalWrite(pinoLEDB1, LOW);
  digitalWrite(pinoLEDR2, HIGH);
  digitalWrite(pinoLEDG2, LOW);
  digitalWrite(pinoLEDB2, LOW);
  digitalWrite(pinoLEDR3, HIGH);
  digitalWrite(pinoLEDG3, LOW);
  digitalWrite(pinoLEDB3, LOW);
  digitalWrite(pinoLEDR4, HIGH);
  digitalWrite(pinoLEDG4, LOW);
  digitalWrite(pinoLEDB4, LOW);
  delay(500);
  noTone(pinoBuzzer);
  digitalWrite(pinoLEDR1, LOW);
  digitalWrite(pinoLEDG1, LOW);
  digitalWrite(pinoLEDB1, LOW);
  digitalWrite(pinoLEDR2, LOW);
  digitalWrite(pinoLEDG2, LOW);
  digitalWrite(pinoLEDB2, LOW);
  digitalWrite(pinoLEDR3, LOW);
  digitalWrite(pinoLEDG3, LOW);
  digitalWrite(pinoLEDB3, LOW);
  digitalWrite(pinoLEDR4, LOW);
  digitalWrite(pinoLEDG4, LOW);
  digitalWrite(pinoLEDB4, LOW);
}

void sensor(){
   // A leitura da temperatura ou umidade pode levar 250ms
  // O atraso do sensor pode chegar a 2 segundos
  temperatura = dht.readTemperature(); // l? a temperatura em Celsius
  umidade = dht.readHumidity(); // l? a umidade
  
  // Se ocorreu alguma falha durante a leitura
  if (isnan(umidade) || isnan(temperatura)) {
    Serial.println("Falha na leitura do Sensor DHT!");
  }
  else { // Se n?o
    Serial.print("Temperatura: ");
    Serial.print(temperatura);
    Serial.print(" *C ");

    Serial.print("\t"); // tabula??o
  
    // Imprime o valor de umidade
    Serial.print("Umidade: ");
    Serial.print(umidade);
    Serial.print(" %\t");
    
    Serial.println(); // nova linha
    if (temperatura > 40 || umidade < 40) {
      // Acende vermelho e aciona buzzer a 1000Hz
      alarm(500, 1000);
      delay(150);
      Serial.print("ALERTA RISCO A SAÚDE! E RISCO DE INCÊNDIO!");
      Serial.println();
      estado = "ALERTA RISCO A SAÚDE! E RISCO DE INCÊNDIO!";
      enviar = (String)temperatura + "," + (String)umidade + "," + estado;
      HC05.println(enviar);
    }
    else if (temperatura < 0) {
      // Acende azul
      digitalWrite(pinoLEDR1, LOW);
      digitalWrite(pinoLEDG1, LOW);
      digitalWrite(pinoLEDB1, HIGH);
      digitalWrite(pinoLEDR2, LOW);
      digitalWrite(pinoLEDG2, LOW);
      digitalWrite(pinoLEDB2, HIGH);
      digitalWrite(pinoLEDR3, LOW);
      digitalWrite(pinoLEDG3, LOW);
      digitalWrite(pinoLEDB3, HIGH);
      Serial.print("Temperatura ambiente muito baixa!");
      Serial.println();
      estado = "Temperatura ambiente muito baixa!";
      enviar = (String)temperatura + "," + (String)umidade + "," + estado;
      HC05.println(enviar);
    }
    else {
      Serial.print("Ambiente agradável!");
      Serial.println();
      estado = "Ambiente agradável!";
      enviar = (String)temperatura + "," + (String)umidade + "," + estado;
      HC05.println(enviar);
    }
  }
}
